# Fritzing sketch LETRERO LED (saved by Fritzing 0.9.3b)

parts:
  Arduino_NANO = Arduino Nano (Rev3.0)
  FUSIBLE_DE_1A = FUSE [package=fuse_5mm]
  REGULADOR_LM7805 = Voltage Regulator [package=78xxl]
  MAX7219 = Matrix LED de 8x8 basada en MAX7219
  D1 = Rectifier Diode [part_number=1N4001 package="300 mil [THT]"]
  MAX7219_2 = Matrix LED de 8x8 basada en MAX7219  # not connected
  Componente3 = Matrix LED de 8x8 basada en MAX7219
  Componente6 = Matrix LED de 8x8 basada en MAX7219
  HC-06 = Bluetooth HC-05 Macho
  part = Resistor [tolerance=±5% resistance=1k package="0603 [SMD]"]
  part_2 = Resistor [tolerance=±5% resistance=220 package="0603 [SMD]"]
  C2 = Electrolytic Capacitor [capacitance=100µF package="200 mil [THT, electrolytic]"]  # not connected
  CONECTOR_PARA_ADAPTADOR_12V = Power Jack [package=power_jack_pth]
  C3 = Electrolytic Capacitor [capacitance=100µF package="200 mil [THT, electrolytic]"]  # not connected

nets:
  N1: Arduino_NANO.D1/TX, part_2.Pin_0
  N2: Arduino_NANO.D0/RX, part.Pin_1
  GND: Arduino_NANO.GND, REGULADOR_LM7805.GND, HC-06.GND
  N3: Arduino_NANO.D2, part.Pin_0
  N4: Arduino_NANO.D10, MAX7219.CS
  N5: Arduino_NANO.D11/MOSI, MAX7219.DIN
  N6: Arduino_NANO.VIN, REGULADOR_LM7805.OUT
  5V: Arduino_NANO.5V, MAX7219.VCC
  N7: Arduino_NANO.D13/SCK, MAX7219.CLK
  N8: FUSIBLE_DE_1A.1, CONECTOR_PARA_ADAPTADOR_12V.PWR
  N9: MAX7219.VCC(OUT), Componente3.VCC
  N10: MAX7219.GND#6, Componente3.GND
  N11: MAX7219.CS(OUT), Componente3.CS
  N12: MAX7219.CLK(OUT), Componente3.CLK
  N13: MAX7219.DOUT, Componente3.DIN
  N14: D1.cathode, CONECTOR_PARA_ADAPTADOR_12V.GNDBREAK
  N15: Componente3.VCC(OUT), Componente6.VCC
  N16: HC-06.RXD, part_2.Pin_1

notes:
  MEKATRONIK 2017
  LETRERO LED + BLUETOOTH+APP ANDROID
  SE CONTINÚA LA CONEXIÓN EXACTAMENTE CON LAS OTRAS 4 MATRICES
